# Fritzing sketch servo_and_ultrasonic_wiring (saved by Fritzing 0.9.10b)
breadboards: 1

parts:
  M1 = Calliope Mini V 1.3
  VCC2 = Battery Pack 3v / 4,5v
  J1 = Basic Servo
  J2 = Basic Servo
  HC-SR04_Sensor_1 = HC-SR04 Ultrasonic Distance Sensor

nets:
  N1: M1.C2, M1.P2, J2.pulse
  N2: M1.C0, M1.P0, HC-SR04_Sensor_1.TRIG
  N3: M1.C1, M1.P1, J1.pulse
  N4: M1.P3, HC-SR04_Sensor_1.ECHO
  GND: VCC2.-, J1.gnd, J2.gnd, HC-SR04_Sensor_1.GND
  VCC: VCC2.+_(3v), J1.vcc, J2.vcc, HC-SR04_Sensor_1.VCC

notes:
  Servo left
  Servo right

custom parts:
  Battery Pack 3v / 4,5v: Your standard 3x AA battery pack (3 Volts / 4,5 Volts)
