# Fritzing sketch servo_wiring (saved by Fritzing 0.9.10b)
breadboards: 1

parts:
  VCC2 = Battery Pack 3v / 4,5v
  J1 = Basic Servo
  J2 = Basic Servo
  M1 = Calliope Mini V 1.3

nets:
  GND: VCC2.-, J1.gnd, J2.gnd, M1.GND, M1.GND_(BAT-)
  VCC: VCC2.+_(3v), J1.vcc, J2.vcc
  N1: J1.pulse, M1.C1, M1.P1
  N2: J2.pulse, M1.C2, M1.P2

notes:
  Servo left
  Servo right

custom parts:
  Battery Pack 3v / 4,5v: Your standard 3x AA battery pack (3 Volts / 4,5 Volts)
