# Fritzing sketch ultrasonic_wiring_pin_header (saved by Fritzing 0.9.10b)
breadboards: 1

parts:
  M1 = Calliope Mini V 1.3
  VCC2 = Battery Pack 3v / 4,5v
  HC-SR04_Sensor_1 = HC-SR04 Ultrasonic Distance Sensor

nets:
  N1: M1.C0, HC-SR04_Sensor_1.TRIG
  N2: M1.GND, M1.GND_(BAT-), VCC2.-
  N3: M1.C3, M1.P3, HC-SR04_Sensor_1.ECHO
  N4: VCC2.+_(3v), HC-SR04_Sensor_1.VCC

custom parts:
  Battery Pack 3v / 4,5v: Your standard 3x AA battery pack (3 Volts / 4,5 Volts)
